// Logisim project bmp59.circ as structural Verilog: 8 circuits, main circuit main
module main (
);

  wire ALU, branch_bool, branched, button_1_out, Clock, clock_1_out, Display, extend_bool, Halt, imm_bool,
       Mem, not_1_out, not_2_out, PC, RegWrite, RS_Bool, RT_Bool, Shamt_Bool;
  wire [0:0] Op_SubOp;
  wire [1:0] PCSrc;
  wire [2:0] RS, RT;
  wire [3:0] branchdecoder_1_bnez, OP, register_1_q_2, Shamt;
  wire [7:0] Imm, multiplexer_1_out, multiplexer_2_out, PC_1, PC_q;
  wire [11:0] register_1_q;
  wire [15:0] ALU_output, bit_extender_1_out, bit_extender_2_out, InstrMem, multiplexer_3_out,
       multiplexer_4_out, ram_1_data, register_file_1_output_reg2, RS_Val, Value;

  Clock clock_1 (.out(clock_1_out));
  Button button_1 (.out(button_1_out));
  Multiplexer #(.select(2), .width(8)) multiplexer_1 (
    .in0(PC_1), .in1(Imm), .in2(RS_Val[7:0]), .in3(multiplexer_2_out), .out(multiplexer_1_out), .sel(PCSrc));  // open: en
  not not_1 (not_1_out, Halt);
  Multiplexer #(.width(8), .enable("false")) multiplexer_2 (
    .in0(PC_1), .in1(Imm), .out(multiplexer_2_out), .sel(branched));
  or or_1 (Clock, clock_1_out, button_1_out);
  Register u_PC (.D(multiplexer_1_out), .en(not_1_out), .Q(PC_q), .clk(Clock));  // open: clr
  Adder adder_1 (.a(PC_q), .b(8'h1), .out(PC_1));  // open: cin, cout
  ROM #(.dataWidth(16)) rom_1 (.addr(PC_q), .data(InstrMem));  // open: sel
  LED led_1 (.in(Halt));
  OpDecoder5 opdecoder5_1 (
    .Op3(OP[3]), .Op2(OP[2]), .Op1(OP[1]), .Op0(OP[0]), .Sub(Op_SubOp[0]), .rt(RT_Bool), .rs(RS_Bool),
    .shamt(Shamt_Bool), .extend(extend_bool), .imm(imm_bool), .branch(branch_bool), .halt(Halt),
    .MemWrite(Mem), .ALU(ALU), .RegWrite(RegWrite), .Display(Display), .PC(PC));
  assign bit_extender_1_out = {{8{1'b0}}, Imm};  // Bit_Extender bit_extender_1
  assign bit_extender_2_out = {{8{Imm[7]}}, Imm};  // Bit_Extender bit_extender_2
  InstrDecode Instruction_Decoder (
    .Instruction_Signal(InstrMem), .OP(OP), .RS(RS), .Sub(Op_SubOp[0]), .Imm(Imm), .Shamt(Shamt), .RT(RT));
  Register_File register_file_1 (
    .Clock(Clock), .Input(Value), .RegEnable(RegWrite), .Write_Read(RS), .Read_Select_2(RT),
    .Output_Reg1(RS_Val), .Output_Reg2(register_file_1_output_reg2));
  not not_2 (not_2_out, Op_SubOp[0]);
  Multiplexer #(.width(16), .enable("false")) multiplexer_3 (
    .in0(register_file_1_output_reg2), .in1(multiplexer_4_out), .out(multiplexer_3_out), .sel(imm_bool));
  Multiplexer #(.width(16), .enable("false")) multiplexer_4 (
    .in0(bit_extender_1_out), .in1(bit_extender_2_out), .out(multiplexer_4_out), .sel(not_2_out));
  Hex_Digit_Display hex_digit_display_1 (.value(register_1_q_2));  // open: dp
  RAM #(.dataWidth(16), .bus("separate")) ram_1 (
    .addr(register_file_1_output_reg2[7:0]), .din(RS_Val), .data(ram_1_data), .str(Mem), .clk(Clock));  // open: sel, ld, clr
  ALU u_ALU (
    .Input1(RS_Val), .Input2(multiplexer_3_out), .OP_SubOp({OP, Op_SubOp[0]}), .Shamt(Shamt), .PC_1(PC_1),
    .Output(ALU_output));
  Hex_Digit_Display hex_digit_display_2 (.value(register_1_q[11:8]));  // open: dp
  Hex_Digit_Display hex_digit_display_3 (.value(register_1_q[7:4]));  // open: dp
  Register #(.width(16)) register_1 (
    .D(RS_Val), .en(Display), .Q({register_1_q_2, register_1_q}), .clk(Clock));  // open: clr
  Hex_Digit_Display hex_digit_display_4 (.value(register_1_q[3:0]));  // open: dp
  BranchDecoder branchdecoder_1 (
    .Op3(OP[3]), .Op2(OP[2]), .Op1(OP[1]), .Op0(OP[0]), .Sub(Op_SubOp[0]), .bgtz(branchdecoder_1_bnez[3]),
    .beqz(branchdecoder_1_bnez[2]), .bltz(branchdecoder_1_bnez[1]), .bnez(branchdecoder_1_bnez[0]));
  Multiplexer #(.width(16), .enable("false")) multiplexer_5 (
    .in0(ram_1_data), .in1(ALU_output), .out(Value), .sel(ALU));
  PCDeocder pcdeocder_1 (
    .Op3(OP[3]), .Op2(OP[2]), .Op1(OP[1]), .Op0(OP[0]), .Sub(Op_SubOp[0]), .branch(PCSrc[1]), .jump(PCSrc[0]));
  Brancher brancher_1 (.RS(RS_Val), .Branch_Op(branchdecoder_1_bnez), .Did_I_Branch(branched));

  // Other names for the same wires on the sheet: Sub = Op_SubOp[0]; Op_SubOp[4:1] = OP

  // Notes on the sheet:
  //   Instruction Memory
  //   contents of rom_1 (hex, n*v repeats v):
  //   219d 1000 2208 7040 1000 7040 1000 7041 1000 7041 1000 7041 1000
  //   LED
  //   Op/Sub Decoder
  //   Register File
  //   Memory
  //   Branch Decoder
  //   PC DECODER
endmodule

module Register_File (
  input  Clock,
  input  [15:0] Input,
  input  RegEnable,
  input  [2:0] Write_Read,
  input  [2:0] Read_Select_2,
  output [15:0] Output_Reg1,
  output [15:0] Output_Reg2
);

  wire demultiplexer_1_out0, demultiplexer_1_out1, demultiplexer_1_out2, demultiplexer_1_out3,
       demultiplexer_1_out4, demultiplexer_1_out5, demultiplexer_1_out6, demultiplexer_1_out7;
  wire [15:0] Output_0a, Output_1a, Output_2a, Output_3a, Output_4a, Output_5a, Output_6a, Output_7a;

  Demultiplexer #(.select(3), .enable("false")) demultiplexer_1 (
    .out0(demultiplexer_1_out0), .out1(demultiplexer_1_out1), .out2(demultiplexer_1_out2),
    .out3(demultiplexer_1_out3), .out4(demultiplexer_1_out4), .out5(demultiplexer_1_out5),
    .out6(demultiplexer_1_out6), .out7(demultiplexer_1_out7), .in(RegEnable), .sel(Write_Read));
  Register #(.width(16)) r0 (.D(Input), .en(demultiplexer_1_out0), .Q(Output_0a), .clk(Clock));  // open: clr
  Register #(.width(16)) r1 (.D(Input), .en(demultiplexer_1_out1), .Q(Output_1a), .clk(Clock));  // open: clr
  Register #(.width(16)) r2 (.D(Input), .en(demultiplexer_1_out2), .Q(Output_2a), .clk(Clock));  // open: clr
  Register #(.width(16)) r3 (.D(Input), .en(demultiplexer_1_out3), .Q(Output_3a), .clk(Clock));  // open: clr
  Register #(.width(16)) r4 (.D(Input), .en(demultiplexer_1_out4), .Q(Output_4a), .clk(Clock));  // open: clr
  Register #(.width(16)) r5 (.D(Input), .en(demultiplexer_1_out5), .Q(Output_5a), .clk(Clock));  // open: clr
  Register #(.width(16)) r6 (.D(Input), .en(demultiplexer_1_out6), .Q(Output_6a), .clk(Clock));  // open: clr
  Register #(.width(16)) r7 (.D(Input), .en(demultiplexer_1_out7), .Q(Output_7a), .clk(Clock));  // open: clr
  Multiplexer #(.select(3), .width(16), .enable("false")) multiplexer_1 (
    .in0(Output_0a), .in1(Output_1a), .in2(Output_2a), .in3(Output_3a), .in4(Output_4a), .in5(Output_5a),
    .in6(Output_6a), .in7(Output_7a), .out(Output_Reg1), .sel(Write_Read));
  Multiplexer #(.select(3), .width(16), .enable("false")) multiplexer_2 (
    .in0(Output_0a), .in1(Output_1a), .in2(Output_2a), .in3(Output_3a), .in4(Output_4a), .in5(Output_5a),
    .in6(Output_6a), .in7(Output_7a), .out(Output_Reg2), .sel(Read_Select_2));

  // Other names for the same wires on the sheet: Output_0b[15:0] = Output_0a; Output_1b[15:0] = Output_1a;
  //   Output_2b[15:0] = Output_2a; Output_3b[15:0] = Output_3a; Output_4b[15:0] = Output_4a;
  //   Output_5b[15:0] = Output_5a; Output_6b[15:0] = Output_6a; Output_7b[15:0] = Output_7a
endmodule

module InstrDecode (
  input  [15:0] Instruction_Signal,
  output Sub,
  output [7:0] Imm,
  output [3:0] Shamt,
  output [2:0] RT,
  output [3:0] OP,
  output [2:0] RS
);


  assign Imm = Instruction_Signal[8:1];
  assign OP = Instruction_Signal[15:12];
  assign RS = Instruction_Signal[11:9];
  assign RT = Instruction_Signal[8:6];
  assign Shamt = Instruction_Signal[4:1];
  assign Sub = Instruction_Signal[0];
endmodule

module ALU (
  input  [15:0] Input1,
  input  [15:0] Input2,
  input  [4:0] OP_SubOp,
  input  [3:0] Shamt,
  input  [7:0] PC_1,
  output [15:0] Output
);

  wire [15:0] AddOut, AndOut, bit_extender_1_out, jal_out, LeftShiftOut, LeftShiftOutV, LiOut, NorOut,
       RightShiftOut, RightShiftOutV, SubOut;

  assign bit_extender_1_out = {{8{1'b0}}, PC_1};  // Bit_Extender bit_extender_1
  Adder #(.width(16)) adder_1 (.a({16{1'b0}}), .b(Input2), .out(LiOut));  // open: cin, cout
  Adder #(.width(16)) adder_2 (.a(Input1), .b(Input2), .out(AddOut));  // open: cin, cout
  Subtractor #(.width(16)) subtractor_1 (.a(Input1), .b(Input2), .out(SubOut));  // open: bin, bout
  assign AndOut = Input1 & Input2;  // AND_Gate and_1, 16 bits wide
  assign NorOut = ~(Input1 | Input2);  // NOR_Gate nor_1, 16 bits wide
  Shifter #(.width(16)) shifter_1 (.in(Input1), .\dist (Input2[3:0]), .out(LeftShiftOutV));
  Shifter #(.width(16), .shift("lr")) shifter_2 (.in(Input1), .\dist (Input2[3:0]), .out(RightShiftOutV));
  Shifter #(.width(16)) shifter_3 (.in(Input1), .\dist (Shamt), .out(LeftShiftOut));
  Shifter #(.width(16), .shift("lr")) shifter_4 (.in(Input1), .\dist (Shamt), .out(RightShiftOut));
  Adder #(.width(16)) adder_3 (.a({16{1'b0}}), .b(bit_extender_1_out), .out(jal_out));  // open: cin, cout
  Multiplexer #(.select(5), .width(16), .enable("false")) multiplexer_1 (
    .in4(LiOut), .in5(LiOut), .in6(AddOut), .in7(SubOut), .in8(AndOut), .in9(NorOut), .in10(AddOut),
    .in11(AddOut), .in12(AddOut), .in14(LeftShiftOutV), .in15(RightShiftOutV), .in16(LeftShiftOut),
    .in17(RightShiftOut), .in20(jal_out), .out(Output), .sel(OP_SubOp));  // open: in0, in1, in2, in3, in13, in18, in19, in21, in22, in23, in24, in25, in26, in27, in28, in29, in30, in31

  // Other names for the same wires on the sheet: OP[4:0] = OP_SubOp; PCAdd[7:0] = PC_1; Put1[15:0] = Input1;
  //   Put2[15:0] = Input2
endmodule

module PCDeocder (
  input  Op3,
  input  Op2,
  input  Op1,
  input  Op0,
  input  Sub,
  output branch,
  output jump
);

  wire and_1_out, and_2_out, and_3_out, and_4_out, and_5_out, and_6_out, not_1_out;

  and and_1 (and_1_out, Op3, Op0, Sub);
  and and_2 (and_2_out, Op3, Op1, Op0);
  and and_3 (and_3_out, Op3, Op2);
  not not_1 (not_1_out, Sub);
  or or_1 (branch, and_1_out, and_2_out, and_3_out);
  and and_4 (and_4_out, Op3, Op0, not_1_out);
  and and_5 (and_5_out, Op3, Op1);
  and and_6 (and_6_out, Op3, Op2);
  or or_2 (jump, and_4_out, and_5_out, and_6_out);
endmodule

module Brancher (
  input  [15:0] RS,
  input  [3:0] Branch_Op,
  output Did_I_Branch
);

  wire beqz, bgtz, bltz, bnez;

  Comparator #(.width(16)) comparator_1 (.a(RS), .b({16{1'b0}}), .gt(bgtz), .eq(beqz), .lt(bltz));
  not not_1 (bnez, beqz);
  Multiplexer #(.select(4), .enable("false")) multiplexer_1 (
    .in1(bnez), .in2(bltz), .in4(beqz), .in8(bgtz), .out(Did_I_Branch), .sel(Branch_Op));  // open: in0, in3, in5, in6, in7, in9, in10, in11, in12, in13, in14, in15
endmodule

module BranchDecoder (
  input  Op3,
  input  Op2,
  input  Op1,
  input  Op0,
  input  Sub,
  output bgtz,
  output beqz,
  output bltz,
  output bnez
);

  wire not_1_out, not_2_out, not_3_out, not_4_out, not_5_out, not_6_out;

  not not_1 (not_1_out, Op2);
  not not_2 (not_2_out, Sub);
  not not_3 (not_3_out, Op1);
  not not_4 (not_4_out, Op2);
  not not_5 (not_5_out, Op1);
  not not_6 (not_6_out, Sub);
  and and_1 (bgtz, not_1_out, not_2_out);
  and and_2 (beqz, not_3_out, Sub);
  and and_3 (bltz, not_4_out, Sub);
  and and_4 (bnez, not_5_out, not_6_out);
endmodule

module OpDecoder5 (
  input  Op3,
  input  Op2,
  input  Op1,
  input  Op0,
  input  Sub,
  output rt,
  output rs,
  output shamt,
  output extend,
  output imm,
  output branch,
  output halt,
  output MemWrite,
  output ALU,
  output RegWrite,
  output Display,
  output PC
);

  wire and_1_out, and_2_out, and_3_out, and_4_out, and_5_out, and_6_out, and_7_out, and_8_out, and_9_out,
       and_10_out, and_11_out, and_12_out, and_13_out, and_14_out, and_15_out, and_16_out, and_17_out,
       and_18_out, and_21_out, and_22_out, and_23_out, and_24_out, and_25_out, and_26_out, and_27_out,
       and_28_out, and_29_out, not_1_out, not_2_out, not_3_out, not_4_out, not_5_out, not_6_out, not_7_out,
       not_8_out, not_9_out, not_10_out, not_11_out, not_12_out, not_13_out, not_14_out, not_15_out,
       not_16_out, not_17_out, not_18_out, not_19_out, not_20_out, not_21_out, not_22_out, not_23_out,
       not_24_out, not_25_out, not_26_out, not_27_out, not_28_out, not_29_out, not_30_out, not_31_out,
       not_32_out, not_33_out, not_34_out, not_35_out, not_36_out, not_37_out, not_38_out, not_39_out,
       not_40_out, not_41_out;

  not not_1 (not_1_out, Op3);
  not not_2 (not_2_out, Op3);
  not not_3 (not_3_out, Op1);
  not not_4 (not_4_out, Op0);
  not not_5 (not_5_out, Op2);
  not not_6 (not_6_out, Op1);
  not not_7 (not_7_out, Op0);
  not not_8 (not_8_out, Op0);
  not not_9 (not_9_out, Op2);
  not not_10 (not_10_out, Op1);
  not not_11 (not_11_out, Op0);
  not not_12 (not_12_out, Op3);
  not not_13 (not_13_out, Op2);
  not not_14 (not_14_out, Op0);
  not not_15 (not_15_out, Op1);
  not not_16 (not_16_out, Op2);
  not not_17 (not_17_out, Op0);
  not not_18 (not_18_out, Op1);
  not not_19 (not_19_out, Sub);
  and and_1 (and_1_out, Op3, Op1, Op0);
  and and_2 (and_2_out, Op3, Op2);
  not not_20 (not_20_out, Op3);
  not not_21 (not_21_out, Op2);
  not not_22 (not_22_out, Op1);
  not not_23 (not_23_out, Op0);
  not not_24 (not_24_out, Op0);
  not not_25 (not_25_out, Op3);
  not not_26 (not_26_out, Op2);
  not not_27 (not_27_out, Op3);
  not not_28 (not_28_out, Op1);
  not not_29 (not_29_out, Op2);
  not not_30 (not_30_out, Op0);
  not not_31 (not_31_out, Op3);
  not not_32 (not_32_out, Op2);
  not not_33 (not_33_out, Op3);
  not not_34 (not_34_out, Op1);
  not not_35 (not_35_out, Op3);
  not not_36 (not_36_out, Sub);
  not not_37 (not_37_out, Op2);
  not not_38 (not_38_out, Op0);
  not not_39 (not_39_out, Op3);
  not not_40 (not_40_out, Op2);
  not not_41 (not_41_out, Op1);
  and and_3 (and_3_out, Op3, Op0);
  and and_4 (and_4_out, Op3, Op1);
  and and_5 (and_5_out, Op3, Op2);
  and and_6 (and_6_out, not_1_out, Op1, Op0);
  and and_7 (and_7_out, not_2_out, Op2, not_3_out, not_4_out);
  and and_8 (and_8_out, Op3, not_5_out, not_6_out, not_7_out);
  and and_9 (and_9_out, Op3, not_8_out);
  and and_10 (and_10_out, Op2, Op1, Op0);
  and and_11 (and_11_out, Op3, not_9_out, not_10_out, not_11_out);
  and and_12 (and_12_out, not_12_out, not_13_out, Op1, not_14_out);
  and and_13 (and_13_out, Op2, not_15_out, Op0);
  and and_14 (and_14_out, not_16_out, Op1, not_17_out);
  and and_15 (and_15_out, Op2, not_18_out, Op0);
  and and_16 (and_16_out, Op3, Op0, not_19_out);
  and and_17 (and_17_out, Op3, Op1);
  and and_18 (and_18_out, Op3, Op2);
  or or_1 (branch, and_1_out, and_2_out);
  and and_19 (halt, not_20_out, not_21_out, not_22_out, not_23_out);
  and and_20 (MemWrite, Op2, Op1, not_24_out, Sub);
  and and_21 (and_21_out, not_25_out, not_26_out, Op1);
  and and_22 (and_22_out, not_27_out, Op2, not_28_out);
  and and_23 (and_23_out, Op2, Op0);
  and and_24 (and_24_out, Op3, not_29_out, not_30_out);
  and and_25 (and_25_out, not_31_out, not_32_out, Op1);
  and and_26 (and_26_out, not_33_out, Op2, not_34_out);
  and and_27 (and_27_out, not_35_out, Op2, not_36_out);
  and and_28 (and_28_out, Op2, Op0);
  and and_29 (and_29_out, Op3, not_37_out, not_38_out);
  and and_30 (Display, not_39_out, not_40_out, not_41_out, Op0);
  or or_2 (PC, and_3_out, and_4_out, and_5_out);
  or or_3 (rt, and_6_out, and_7_out, and_8_out);
  or or_4 (rs, Sub, Op1, Op2, and_9_out);
  or or_5 (shamt, and_10_out, and_11_out);
  or or_6 (extend, and_12_out, and_13_out);
  or or_7 (imm, and_14_out, and_15_out, and_16_out, and_17_out, and_18_out);
  or or_8 (ALU, and_21_out, and_22_out, and_23_out, and_24_out);
  or or_9 (RegWrite, and_25_out, and_26_out, and_27_out, and_28_out, and_29_out);
endmodule
